// Logisim project Digital_Flight_Control_System.circ as structural Verilog: 9 circuits, main circuit Phase0_Abort
module Phase0_Abort (
  input  F,
  input  T,
  input  S,
  output A
);

  wire and_1_out, and_2_out, and_3_out, clock_1_out, or_1_out;

  and and_1 (and_1_out, F, T);
  and and_2 (and_2_out, T, S);
  and and_3 (and_3_out, S, F);
  or or_1 (or_1_out, and_1_out, and_2_out, and_3_out);
  Clock clock_1 (.out(clock_1_out));
  D_Flip_Flop #(.trigger("high")) D_flip_flop (.clk(clock_1_out), .D(or_1_out), .Q(A));  // open: Qn, preset, en, reset

  // Notes on the sheet:
  //   Fuel
  //   Tilt
  //   Strain
  //   AND
  //   AND
  //   AND
  //   OR
  //   Noise remover
  //   Abort
endmodule

module Phase1_Deploy (
  input  M,
  input  A,
  input  V,
  input  S,
  output D
);

  wire and_1_out;

  Pull_Resistor pull_resistor_1 (.node(A));
  Pull_Resistor pull_resistor_2 (.node(V));
  Pull_Resistor pull_resistor_3 (.node(S));
  and and_1 (and_1_out, A, A, V, S);
  or or_1 (D, M, and_1_out);

  // Notes on the sheet:
  //   Altitude
  //   Velocity
  //   Stability
  //   Manual Override
  //   pull resistor
  //   AND
  //   OR
  //   Deploy Parachute
endmodule

module Phase2_Monitor (
  input  Tilt_A,
  input  decrement,
  input  Tilt_B
);

  wire clock_1_out, comparator_1_eq, comparator_1_gt, reset_out, xor_1_out;
  wire [1:0] Counter_q;

  xor xor_1 (xor_1_out, Tilt_A, Tilt_B);
  LED Fault_Led (.in(xor_1_out));
  Counter #(.width(2), .max('h3)) Counter (
    .load(decrement), .count(xor_1_out), .Q(Counter_q), .clk(clock_1_out), .clr(reset_out));  // open: D, carry
  Button reset (.out(reset_out));
  Clock clock_1 (.out(clock_1_out));
  Comparator #(.width(2), .mode("unsigned")) comparator_1 (
    .a(Counter_q), .b(2'b10), .gt(comparator_1_gt), .eq(comparator_1_eq));  // open: lt
  LED Safe_Mode (.in(comparator_1_gt));

  // Notes on the sheet:
  //   XOR
  //   CLK
  //   Comparator
endmodule

module Phase3_Sequencer (
);

  wire A_q, B_q, clock_1_out, nor_1_out, not_1_out, Reset_out;

  Clock clock_1 (.out(clock_1_out));
  D_Flip_Flop A (.clk(clock_1_out), .D(B_q), .Q(A_q), .reset(Reset_out));  // open: Qn, preset, en
  not not_1 (not_1_out, A_q);
  Button Reset (.out(Reset_out));
  D_Flip_Flop B (.clk(clock_1_out), .D(not_1_out), .Q(B_q), .reset(Reset_out));  // open: Qn, preset, en
  nor nor_1 (nor_1_out, A_q, B_q);
  LED Engine_Ignition (.in(nor_1_out));

  // Notes on the sheet:
  //   CLK
  //   A
  //   Q1
  //   D-Flip flop
  //   B
  //   Q0
  //   D-Flip flop
  //   NOR
endmodule

module Phase4_ParityGenerator (
  input  Q1,
  input  Q2,
  input  Abort,
  input  Safe,
  output Parity
);

  wire xor_1_out, xor_2_out;

  xor xor_1 (xor_1_out, Q1, Q2);
  xor xor_2 (xor_2_out, Abort, Safe);
  xor xor_3 (Parity, xor_1_out, xor_2_out);

  // Notes on the sheet:
  //   XOR
  //   XOR
  //   XOR
endmodule

module Main (
  input  Fuel_Pressure,
  input  Tilt,
  input  in_3,
  input  in_4,
  input  in_5,
  input  Manual_Override,
  input  Altitude,
  input  Velocity,
  input  Stability,
  output Engine_Ignition,
  output Parity,
  output out_12
);

  wire phase0_abort2_1_a, phase2_monitor2_1_out_3, phase3_sequencer2_1_out_2, phase3_sequencer2_1_out_3;

  Phase0_Abort2 phase0_abort2_1 (.F(Fuel_Pressure), .T(Tilt), .S(in_3), .A(phase0_abort2_1_a));
  Phase2_Monitor2 phase2_monitor2_1 (.Tilt_A(in_4), .Tilt_B(in_5), .out_3(phase2_monitor2_1_out_3));
  Phase3_Sequencer2 phase3_sequencer2_1 (
    .out_1(Engine_Ignition), .out_2(phase3_sequencer2_1_out_2), .out_3(phase3_sequencer2_1_out_3));
  Phase1_Deploy phase1_deploy_1 (.M(Manual_Override), .A(Altitude), .V(Velocity), .S(Stability), .D(out_12));
  Phase4_ParityGenerator phase4_paritygenerator_1 (
    .Q1(phase3_sequencer2_1_out_3), .Q2(phase3_sequencer2_1_out_2), .Abort(phase0_abort2_1_a),
    .Safe(phase2_monitor2_1_out_3), .Parity(Parity));

  // Notes on the sheet:
  //   Structural Strain
  //   Deploy
endmodule

module Phase2_Monitor2 (
  input  Tilt_A,
  input  Tilt_B,
  output out_3
);

  wire clock_1_out, comparator_1_eq, reset_out, xor_1_out;
  wire [1:0] Counter_q;

  xor xor_1 (xor_1_out, Tilt_A, Tilt_B);
  LED Fault_Led (.in(xor_1_out));
  Counter #(.width(2), .max('h3)) Counter (
    .count(xor_1_out), .Q(Counter_q), .clk(clock_1_out), .clr(reset_out));  // open: load, D, carry
  Button reset (.out(reset_out));
  Clock clock_1 (.out(clock_1_out));
  Comparator #(.width(2), .mode("unsigned")) comparator_1 (
    .a(Counter_q), .b(2'b10), .gt(out_3), .eq(comparator_1_eq));  // open: lt
  LED Safe_Mode (.in(out_3));

  // Notes on the sheet:
  //   XOR
  //   Comparator
endmodule

module Phase3_Sequencer2 (
  output out_1,
  output out_2,
  output out_3
);

  wire clock_1_out, not_1_out, Reset_out;

  Clock clock_1 (.out(clock_1_out));
  D_Flip_Flop A (.clk(clock_1_out), .D(out_2), .Q(out_3), .reset(Reset_out));  // open: Qn, preset, en
  not not_1 (not_1_out, out_3);
  Button Reset (.out(Reset_out));
  D_Flip_Flop B (.clk(clock_1_out), .D(not_1_out), .Q(out_2), .reset(Reset_out));  // open: Qn, preset, en
  nor nor_1 (out_1, out_3, out_2);
  LED Engine_Ignition (.in(out_1));

  // Notes on the sheet:
  //   A
  //   Q1
  //   B
  //   Q0
endmodule

module Phase0_Abort2 (
  input  F,
  input  T,
  input  S,
  output A
);

  wire and_1_out, and_2_out, and_3_out;

  and and_1 (and_1_out, F, T);
  and and_2 (and_2_out, T, S);
  and and_3 (and_3_out, S, F);
  or or_1 (A, and_1_out, and_2_out, and_3_out);

  // Notes on the sheet:
  //   Fuel
  //   Tilt
  //   Strain
  //   AND
  //   AND
  //   AND
  //   OR
  //   Abort
endmodule
